# Fritzing sketch Remote Control (saved by Fritzing 0.8.3b)
circuit board: 6.64626cm x 5.36222cm
breadboards: 1

parts:
  S2 = Pushbutton [package="[THT]"]
  S3 = Pushbutton [package="[THT]"]
  S4 = Pushbutton [package="[THT]"]
  R1 = Resistor [tolerance=±5% resistance=1k package=THT]
  R2 = Resistor [tolerance=±5% resistance=1k package=THT]
  R3 = Resistor [tolerance=±5% resistance=1k package=THT]
  Parte1 = Arduino Uno (Rev3)
  U1 = XBee
  R4 = Rotary Potentiometer (Small)
  LED1 = LED - 5mm [color="Red (633nm)" package="5 mm [THT]"]
  LED2 = LED - 5mm [color="Green (570nm)" package="5 mm [THT]"]
  R5 = Resistor [tolerance=±5% resistance=330 package=THT]

nets:
  GND: S2.Pin_1, S2.Pin_2, S3.Pin_1, S3.Pin_2, S4.Pin_1, S4.Pin_2, Parte1.GND, U1.GND, R4.leg1, R5.Pin_1
  N1: S2.Pin_3, S2.Pin_4, R3.Pin_1, Parte1.D4
  N2: S3.Pin_3, S3.Pin_4, R2.Pin_1, Parte1.D3_PWM
  N3: S4.Pin_3, S4.Pin_4, R1.Pin_1, Parte1.D2
  N4: R1.Pin_0, R2.Pin_0, R3.Pin_0, Parte1.5V
  N5: Parte1.A0, R4.wiper
  N6: Parte1.D0/RX, U1.pin2
  N7: Parte1.D1/TX, U1.pin3
  N8: Parte1.D6_PWM, LED2.anode
  N9: Parte1.D7, LED1.anode
  3V3: Parte1.3V3, U1.VCC
  N10: Parte1.VIN, R4.leg2
  N11: LED1.cathode, LED2.cathode, R5.Pin_0
